# Fritzing sketch v0.1 (saved by Fritzing 0.8.7b)
circuit board: 9.67999cm x 4.09864cm
breadboards: 1

parts:
  IC3 = SO08 [chip_label=IC package=SO]
  XTAL1 = Crystal [frequency="16 Mhz" package=THT]
  XTAL2 = Crystal [frequency="8 MHz" package=THT]
  D2 = Rectifier Diode [part_number=1N4001 package="300 mil [THT]"]
  C1 = Ceramic Capacitor [capacitance=100nF package="100 mil [THT, multilayer]"]
  U2 = MCP73831 [package=sot23-5]
  R1 = Resistor [tolerance=±5% resistance=220 package=THT]
  D3 = Rectifier Diode [part_number=1N4001 package="300 mil [THT]"]
  J1 = female pin header, 2 pins [form="♀ (female)"]
  CONN1 = USB connector [package=THT]
  R2 = Resistor [tolerance=±5% resistance=47 package=THT]
  R3 = Resistor [tolerance=±5% resistance=47 package=THT]
  R4 = Resistor [tolerance=±5% resistance=1.5k package=THT]
  C2 = Ceramic Capacitor [capacitance=100nF package="100 mil [THT, multilayer]"]
  C3 = Ceramic Capacitor [capacitance=100nF package="100 mil [THT, multilayer]"]
  C4 = Ceramic Capacitor [capacitance=100nF package="100 mil [THT, multilayer]"]
  Part1 = SO20W [chip_label=IC package=SO20W]
  Part2 = SO20W [chip_label=IC package=SO20W]
  C5 = Ceramic Capacitor [capacitance=10pF package="100 mil [THT, multilayer]"]
  C6 = Ceramic Capacitor [capacitance=10pF package="100 mil [THT, multilayer]"]
  J4 = female pin header, 2 pins [form="♀ (female)"]
  D4 = Rectifier Diode [part_number=1N4001 package="300 mil [THT]"]
  R5 = Resistor [tolerance=±5% resistance=220 package=THT]
  C7 = Ceramic Capacitor [capacitance=100nF package="100 mil [THT, multilayer]"]
  J5 = female pin header, 2 pins [form="♀ (female)"]
  D5 = Rectifier Diode [part_number=1N4001 package="300 mil [THT]"]
  J6 = female pin header, 2 pins [form="♀ (female)"]
  J7 = female pin header, 2 pins [form="♀ (female)"]
  IC2 = SO08 [chip_label=IC package=SO]
  Q1 = NPN-Transistor [package="TO92 [THT]"]  # not connected
  R6 = Resistor [tolerance=±5% resistance=4.7k package=THT]
  D6 = Rectifier Diode [part_number=1N4001 package="300 mil [THT]"]
  Bluetooth1 = Bluetooth UART SMD module

nets:
  RAM-CS: IC3.1, Part2.PD2
  MCU-SI / Flash-SO: IC3.2, Part1.PB6, Part2.PB5, IC2.2
  GND: IC3.4, C1.1, U2.VSS, R1.Pin_1, J1.pin2, CONN1.GND, CONN1.chassis5, C2.0, C3.0, C4.1, Part1.GND, Part2.GND, C5.0, C6.0, J4.pin2, C7.0, J5.pin2, J6.pin2, J7.pin2, IC2.4, D6.anode, Bluetooth1.GND
  MCU-SO / Flash-SI: IC3.5, Part1.PB5, Part2.PB6, IC2.5
  SCK: IC3.6, Part1.PB7, Part2.PB7, IC2.6
  N1: IC3.7, IC3.8, D4.anode, D5.anode
  N2: XTAL1.pin_0, C2.1, Part1.PA1
  N3: XTAL1.pin_1, C3.1, Part1.PA0
  N4: XTAL2.pin_0, Part2.PA1, C6.1
  N5: XTAL2.pin_1, Part2.PA0, C5.1
  N6: D2.cathode, C1.0, U2.VIN
  N7: D2.anode, CONN1.5V
  N8: U2.VBAT, D3.anode, J1.pin1, C4.0
  N9: U2.PROG, R1.Pin_0
  N10: D3.cathode, Part1.Vcc, J4.pin1
  N11: CONN1.d-, R3.Pin_0, R4.Pin_0
  N12: CONN1.d+, R2.Pin_0
  N13: R2.Pin_1, Part1.PD3
  N14: R3.Pin_1, Part1.PD5
  N15: R4.Pin_1, Part1.PD4
  Flash-CS: Part1.PB4, Part2.PD3, IC2.1
  N16: Part2.RxD, Bluetooth1.UART_Rx
  N17: Part2.TxD, Bluetooth1.UART_Tx
  N18: Part2.PB4, R5.Pin_0
  VCC: Part2.Vcc, D5.cathode, J6.pin1, Bluetooth1.Vcc
  N19: D4.cathode, J7.pin1, IC2.3, IC2.7, IC2.8
  N20: R5.Pin_1, C7.1
  N21: J5.pin1, R6.Pin_1, D6.cathode

custom parts:
  Bluetooth UART SMD module: Bluetooth UART SMD module: HM-10, BC-04, etc.
