# Fritzing sketch v0.2 (saved by Fritzing 0.9.0b)
circuit board: 3.5cm x 1.7cm
breadboards: 1

parts:
  IC1 = QFN-20-0.4MM [chip_label=IC package=QFN]
  U1 = MCP73831 [package=sot23-5]
  Y1 = CRYSTAL [package=crystal-32khz-smd]
  Bluetooth1 = Bluetooth UART SMD module
  U2 = Mini-USB _B_ connector with 5th pin broken out. [package=usb-minib]
  U3 = MMDT3904 [package=sot363]
  Part2 = S25FL204K as SO08 [part_number=S25FL204K chip_label=IC package=SO08]
  C3 = Ceramic Capacitor [capacitance=10pF package="0603 [SMD, multilayer]"]
  C5 = Ceramic Capacitor [capacitance=100nF package="0603 [SMD, multilayer]"]
  D1 = Diode [package=sod523]
  R1 = Resistor [tolerance=±5% package="0402 [SMD]"]
  C6 = Ceramic Capacitor [capacitance=10pF package="0603 [SMD, multilayer]"]
  C4 = Ceramic Capacitor [capacitance="100 nF" package="0603 [SMD, multilayer]"]
  C7 = Ceramic Capacitor [capacitance=10pF package="0603 [SMD, multilayer]"]
  R2 = Resistor [tolerance=±5% package="0402 [SMD]"]
  J1 = rounded female pin header, 2 pins [form="♀ (female rounded)"]
  Part3 = 23K256-IS/N in SO08 Package [part_number=23K256-IS/N chip_label=IC package=SO08]

nets:
  N1: IC1.2, Bluetooth1.UART_Rx
  N2: IC1.3, Bluetooth1.UART_Tx
  N3: IC1.4, Y1.2, C3.1
  N4: IC1.5, Y1.1, C4.1
  GND: IC1.10, U1.VSS, Bluetooth1.GND, Bluetooth1.PIO4, Bluetooth1.PIO5, U2.VBUS, U3.G$1_E, Part2.GND, C3.0, C5.1, R1.Pin_1, C6.1, C4.0, C7.1, J1.pin2, Part3.GND
  N5: IC1.14, Part2.CS
  N6: IC1.15, Part3.CS
  N7: IC1.16, R2.Pin_0
  N8: IC1.17, Part2.SO, Part3.SO
  N9: IC1.18, Part2.SI, Part3.SI
  N10: IC1.19, Part2.SCK, Part3.SCK
  3.3V: IC1.20, U1.VBAT, Bluetooth1.Vcc, Part2.WP, Part2.HOLD, Part2.Vcc, C6.0, Part3.HOLD, Part3.Vcc
  N11: U1.VIN, C5.0, D1.C
  N12: U1.PROG, R1.Pin_0
  N13: U2.GND, D1.A
  N14: U3.G$1_C, J1.pin1
  N15: U3.G$1_B, C7.0, R2.Pin_1

custom parts:
  Bluetooth UART SMD module: Bluetooth UART SMD module: HM-10, BC-04, etc.
